// Logisim project d8421_5.circ as structural Verilog: 1 circuit, main circuit main
module main (
  input  [3:0] in_1,
  input  [3:0] in_2,
  output [3:0] out_3,
  output [3:0] out_4,
  output [3:0] out_5,
  output [3:0] out_6
);

  wire and_6_out, and_7_out, and_8_out, and_9_out, and_10_out, and_11_out, not_1_out, not_2_out, not_3_out,
       not_4_out, not_5_out, not_6_out, not_7_out, not_8_out, or_1_out, or_2_out, or_3_out, or_4_out,
       or_5_out, or_6_out, or_7_out, or_8_out, or_9_out, or_10_out, or_11_out, or_12_out, or_13_out;

  not not_1 (not_1_out, in_1[1]);
  not not_2 (not_2_out, in_1[3]);
  not not_3 (not_3_out, in_1[0]);
  not not_4 (not_4_out, in_1[2]);
  or or_1 (or_1_out, in_1[2], in_1[1]);
  or or_2 (or_2_out, in_1[3], not_1_out, in_1[0]);
  or or_3 (or_3_out, in_1[3], not_4_out, not_3_out);
  or or_4 (or_4_out, not_2_out, in_1[2], in_1[1], in_1[0]);
  or or_5 (or_5_out, in_1[3], not_4_out);
  or or_6 (or_6_out, in_1[3], not_1_out, not_3_out);
  or or_7 (or_7_out, in_1[3], in_1[2], not_1_out, not_3_out);
  or or_8 (or_8_out, not_2_out, in_1[2], in_1[1], not_3_out);
  or or_9 (or_9_out, in_1[3], in_1[1], in_1[0]);
  or or_10 (or_10_out, in_1[3], not_4_out, in_1[1]);
  or or_11 (or_11_out, in_1[3], not_4_out, in_1[0]);
  or or_12 (or_12_out, in_1[2], in_1[1], not_3_out);
  or or_13 (or_13_out, in_1[3], not_3_out);
  and and_1 (out_4[3], or_1_out, or_2_out, or_3_out);
  and and_2 (out_4[2], or_4_out, or_5_out, or_6_out);
  and and_3 (out_4[1], or_7_out, or_8_out, or_9_out, or_10_out, or_11_out);
  and and_4 (out_4[0], or_12_out, or_13_out);
  // Probe on in_2
  not not_5 (not_5_out, in_2[3]);
  not not_6 (not_6_out, in_2[1]);
  not not_7 (not_7_out, in_2[2]);
  not not_8 (not_8_out, in_2[0]);
  and and_5 (out_6[3], not_5_out, in_2[2], not_6_out);
  and and_6 (and_6_out, not_5_out, not_7_out, in_2[0]);
  and and_7 (and_7_out, not_5_out, not_7_out, in_2[1]);
  and and_8 (and_8_out, not_5_out, not_7_out, in_2[1]);
  and and_9 (and_9_out, in_2[3], not_7_out, not_6_out);
  and and_10 (and_10_out, not_5_out, in_2[0]);
  and and_11 (and_11_out, not_7_out, not_6_out, in_2[0]);
  or or_14 (out_6[2], and_6_out, and_7_out);
  or or_15 (out_6[1], and_8_out, and_9_out);
  or or_16 (out_6[0], and_10_out, and_11_out);
  // Probe on out_6

  assign out_3 = in_1;
  assign out_5 = out_4;
endmodule
