// Logisim project ods3.circ as structural Verilog: 1 circuit, main circuit main
module main (
  input  [7:0] in_1,
  input  A,
  input  [7:0] in_3,
  input  B,
  input  C,
  input  [7:0] in_6,
  output out_7,
  output out_8,
  output [7:0] out_9,
  output out_10
);

  wire and_1_out, and_2_out, and_3_out, and_4_out, and_5_out, and_6_out, and_7_out, and_8_out, and_9_out,
       and_10_out, and_11_out, and_12_out, and_13_out, and_14_out, and_15_out, and_16_out, and_17_out,
       and_18_out, and_19_out, and_20_out, and_21_out, and_22_out, and_23_out, and_24_out, and_25_out,
       and_26_out, and_27_out, and_28_out, and_29_out, and_30_out, and_31_out, and_32_out, and_33_out,
       and_34_out, and_35_out, and_36_out, and_37_out, and_38_out, and_39_out, and_40_out, and_41_out,
       and_42_out, and_43_out, and_44_out, and_45_out, and_46_out, and_47_out, and_48_out, and_49_out,
       and_50_out, and_51_out, and_52_out, and_53_out, and_54_out, and_55_out, and_56_out, and_57_out,
       and_58_out, and_59_out, and_60_out, and_61_out, and_62_out, and_63_out, nA_2_out, nA_3_out, nA_4_out,
       nA_5_out, nA_6_out, nA_7_out, nA_8_out, nA_9_out, nA_out, nB_2_out, nB_3_out, nB_4_out, nB_5_out,
       nB_6_out, nB_7_out, nB_8_out, nB_9_out, nB_out, nC_out, not_1_out, not_2_out, not_3_out, not_4_out,
       not_5_out, not_6_out, not_7_out, not_8_out, or_3_out, or_5_out, or_7_out, or_9_out, or_11_out,
       or_13_out, or_15_out;

  not nA (nA_out, A);
  not nB (nB_out, B);
  not nC (nC_out, C);
  and and_1 (and_1_out, nA_out, nB_out, C);
  and and_2 (and_2_out, nA_out, B, nC_out);
  and and_3 (and_3_out, A, nB_out, nC_out);
  and and_4 (and_4_out, A, B, C);
  and and_5 (and_5_out, A, B);
  and and_6 (and_6_out, A, C);
  and and_7 (and_7_out, B, C);
  or or_1 (out_8, and_1_out, and_2_out, and_3_out, and_4_out);
  or or_2 (out_7, and_5_out, and_6_out, and_7_out);
  // Probe on in_6
  // Probe on in_1
  not nA_2 (nA_2_out, in_6[0]);
  not nB_2 (nB_2_out, in_1[0]);
  not not_1 (not_1_out, 1'b0);
  not nA_3 (nA_3_out, in_6[1]);
  not nB_3 (nB_3_out, in_1[1]);
  not not_2 (not_2_out, or_3_out);
  not nA_4 (nA_4_out, in_6[2]);
  not nB_4 (nB_4_out, in_1[2]);
  not not_3 (not_3_out, or_5_out);
  not nA_5 (nA_5_out, in_6[3]);
  not nB_5 (nB_5_out, in_1[3]);
  not not_4 (not_4_out, or_7_out);
  not nA_6 (nA_6_out, in_6[4]);
  not nB_6 (nB_6_out, in_1[4]);
  not not_5 (not_5_out, or_9_out);
  not nA_7 (nA_7_out, in_6[5]);
  not nB_7 (nB_7_out, in_1[5]);
  not not_6 (not_6_out, or_11_out);
  not nA_8 (nA_8_out, in_6[6]);
  not nB_8 (nB_8_out, in_1[6]);
  not not_7 (not_7_out, or_13_out);
  not nA_9 (nA_9_out, in_6[7]);
  not nB_9 (nB_9_out, in_1[7]);
  not not_8 (not_8_out, or_15_out);
  and and_8 (and_8_out, in_6[0], in_1[0]);
  and and_9 (and_9_out, in_6[0], 1'b0);
  and and_10 (and_10_out, in_1[0], 1'b0);
  and and_11 (and_11_out, nA_2_out, nB_2_out, 1'b0);
  and and_12 (and_12_out, nA_2_out, in_1[0], not_1_out);
  and and_13 (and_13_out, in_6[0], nB_2_out, not_1_out);
  and and_14 (and_14_out, in_6[0], in_1[0], 1'b0);
  and and_15 (and_15_out, in_6[1], in_1[1]);
  and and_16 (and_16_out, in_6[1], or_3_out);
  and and_17 (and_17_out, in_1[1], or_3_out);
  and and_18 (and_18_out, nA_3_out, nB_3_out, or_3_out);
  and and_19 (and_19_out, nA_3_out, in_1[1], not_2_out);
  and and_20 (and_20_out, in_6[1], nB_3_out, not_2_out);
  and and_21 (and_21_out, in_6[1], in_1[1], or_3_out);
  and and_22 (and_22_out, in_6[2], in_1[2]);
  and and_23 (and_23_out, in_6[2], or_5_out);
  and and_24 (and_24_out, in_1[2], or_5_out);
  and and_25 (and_25_out, nA_4_out, nB_4_out, or_5_out);
  and and_26 (and_26_out, nA_4_out, in_1[2], not_3_out);
  and and_27 (and_27_out, in_6[2], nB_4_out, not_3_out);
  and and_28 (and_28_out, in_6[2], in_1[2], or_5_out);
  and and_29 (and_29_out, in_6[3], in_1[3]);
  and and_30 (and_30_out, in_6[3], or_7_out);
  and and_31 (and_31_out, in_1[3], or_7_out);
  and and_32 (and_32_out, nA_5_out, nB_5_out, or_7_out);
  and and_33 (and_33_out, nA_5_out, in_1[3], not_4_out);
  and and_34 (and_34_out, in_6[3], nB_5_out, not_4_out);
  and and_35 (and_35_out, in_6[3], in_1[3], or_7_out);
  and and_36 (and_36_out, in_6[4], in_1[4]);
  and and_37 (and_37_out, in_6[4], or_9_out);
  and and_38 (and_38_out, in_1[4], or_9_out);
  and and_39 (and_39_out, nA_6_out, nB_6_out, or_9_out);
  and and_40 (and_40_out, nA_6_out, in_1[4], not_5_out);
  and and_41 (and_41_out, in_6[4], nB_6_out, not_5_out);
  and and_42 (and_42_out, in_6[4], in_1[4], or_9_out);
  and and_43 (and_43_out, in_6[5], in_1[5]);
  and and_44 (and_44_out, in_6[5], or_11_out);
  and and_45 (and_45_out, in_1[5], or_11_out);
  and and_46 (and_46_out, nA_7_out, nB_7_out, or_11_out);
  and and_47 (and_47_out, nA_7_out, in_1[5], not_6_out);
  and and_48 (and_48_out, in_6[5], nB_7_out, not_6_out);
  and and_49 (and_49_out, in_6[5], in_1[5], or_11_out);
  and and_50 (and_50_out, in_6[6], in_1[6]);
  and and_51 (and_51_out, in_6[6], or_13_out);
  and and_52 (and_52_out, in_1[6], or_13_out);
  and and_53 (and_53_out, nA_8_out, nB_8_out, or_13_out);
  and and_54 (and_54_out, nA_8_out, in_1[6], not_7_out);
  and and_55 (and_55_out, in_6[6], nB_8_out, not_7_out);
  and and_56 (and_56_out, in_6[6], in_1[6], or_13_out);
  and and_57 (and_57_out, in_6[7], in_1[7]);
  and and_58 (and_58_out, in_6[7], or_15_out);
  and and_59 (and_59_out, in_1[7], or_15_out);
  and and_60 (and_60_out, nA_9_out, nB_9_out, or_15_out);
  and and_61 (and_61_out, nA_9_out, in_1[7], not_8_out);
  and and_62 (and_62_out, in_6[7], nB_9_out, not_8_out);
  and and_63 (and_63_out, in_6[7], in_1[7], or_15_out);
  or or_3 (or_3_out, and_8_out, and_9_out, and_10_out);
  or or_4 (out_9[0], and_11_out, and_12_out, and_13_out, and_14_out);
  or or_5 (or_5_out, and_15_out, and_16_out, and_17_out);
  or or_6 (out_9[1], and_18_out, and_19_out, and_20_out, and_21_out);
  or or_7 (or_7_out, and_22_out, and_23_out, and_24_out);
  or or_8 (out_9[2], and_25_out, and_26_out, and_27_out, and_28_out);
  or or_9 (or_9_out, and_29_out, and_30_out, and_31_out);
  or or_10 (out_9[3], and_32_out, and_33_out, and_34_out, and_35_out);
  or or_11 (or_11_out, and_36_out, and_37_out, and_38_out);
  or or_12 (out_9[4], and_39_out, and_40_out, and_41_out, and_42_out);
  or or_13 (or_13_out, and_43_out, and_44_out, and_45_out);
  or or_14 (out_9[5], and_46_out, and_47_out, and_48_out, and_49_out);
  or or_15 (or_15_out, and_50_out, and_51_out, and_52_out);
  or or_16 (out_9[6], and_53_out, and_54_out, and_55_out, and_56_out);
  or or_17 (out_10, and_57_out, and_58_out, and_59_out);
  or or_18 (out_9[7], and_60_out, and_61_out, and_62_out, and_63_out);
  // Probe on out_9

  // Notes on the sheet:
  //   A
  //   B
  //   !A
  //   C
  //   !C
  //   !B
endmodule
