// Logisim project t_trigger_sch.circ as structural Verilog: 1 circuit, main circuit main
module main (
  input  in_1,
  input  in_2,
  output [3:0] out_3
);

  wire and_1_out, and_2_out, nand_1_out, nand_2_out, nand_3_out, nand_4_out, nand_5_out, nand_6_out,
       nand_7_out, nand_8_out, nand_9_out, nand_10_out, nand_11_out, nand_12_out, nand_13_out, nand_14_out,
       nand_15_out, nand_16_out, nand_17_out, nand_18_out, nand_19_out, nand_20_out, nand_21_out,
       nand_22_out, nand_23_out, nand_24_out, nand_26_out, nand_28_out, nand_30_out, nand_32_out;

  and and_1 (and_1_out, nand_32_out, nand_30_out, nand_28_out);
  and and_2 (and_2_out, nand_32_out, nand_30_out);
  nand nand_1 (nand_1_out, nand_26_out, in_1, and_1_out);
  nand nand_2 (nand_2_out, and_1_out, in_1, out_3[3]);
  nand nand_3 (nand_3_out, nand_28_out, in_1, and_2_out);
  nand nand_4 (nand_4_out, and_2_out, in_1, out_3[2]);
  nand nand_5 (nand_5_out, nand_30_out, in_1, nand_32_out);
  nand nand_6 (nand_6_out, nand_32_out, in_1, out_3[1]);
  nand nand_7 (nand_7_out, nand_32_out, 1'b1, in_1);
  nand nand_8 (nand_8_out, in_1, 1'b1, out_3[0]);
  nand nand_9 (nand_9_out, nand_1_out, nand_10_out);
  nand nand_10 (nand_10_out, nand_9_out, nand_2_out);
  nand nand_11 (nand_11_out, nand_3_out, nand_12_out);
  nand nand_12 (nand_12_out, nand_11_out, nand_4_out);
  nand nand_13 (nand_13_out, nand_5_out, nand_14_out);
  nand nand_14 (nand_14_out, nand_13_out, nand_6_out);
  nand nand_15 (nand_15_out, nand_7_out, nand_16_out);
  nand nand_16 (nand_16_out, nand_15_out, nand_8_out);
  nand nand_17 (nand_17_out, nand_1_out, nand_9_out);
  nand nand_18 (nand_18_out, nand_10_out, nand_2_out);
  nand nand_19 (nand_19_out, nand_3_out, nand_11_out);
  nand nand_20 (nand_20_out, nand_12_out, nand_4_out);
  nand nand_21 (nand_21_out, nand_5_out, nand_13_out);
  nand nand_22 (nand_22_out, nand_14_out, nand_6_out);
  nand nand_23 (nand_23_out, nand_7_out, nand_15_out);
  nand nand_24 (nand_24_out, nand_16_out, nand_8_out);
  nand nand_25 (out_3[3], nand_17_out, nand_26_out);
  nand nand_26 (nand_26_out, out_3[3], nand_18_out);
  nand nand_27 (out_3[2], nand_19_out, nand_28_out);
  nand nand_28 (nand_28_out, out_3[2], nand_20_out);
  nand nand_29 (out_3[1], nand_21_out, nand_30_out);
  nand nand_30 (nand_30_out, out_3[1], nand_22_out);
  nand nand_31 (out_3[0], nand_23_out, nand_32_out);
  nand nand_32 (nand_32_out, out_3[0], nand_24_out);
endmodule
